// Logisim project ALU.circ as structural Verilog
module ALU (
  input  [31:0] A,
  input  [31:0] B,
  input  [3:0] \Operación ,
  input  Enable,
  output [31:0] Salida,
  output out_6,
  output out_7,
  output out_8,
  output [31:0] Acarreo
);

  wire CarryAdd, CarrySub, comparator_1_gt, comparator_2_lt;
  wire [31:0] AND, bit_extender_3_out, bit_extender_4_out, C_M, Comp_Mayor, Comp_Menor, \División ,
       \Multiplicación , NOT_A, NOT_B, OR, Resta, Resto, Suma, XOR;

  Adder #(.width(32)) adder_1 (.a(A), .b(B), .out(Suma), .cout(CarryAdd));  // open: cin
  Subtractor #(.width(32)) subtractor_1 (.a(A), .b(B), .out(Resta), .bout(CarrySub));  // open: bin
  Multiplier #(.width(32)) multiplier_1 (.a(A), .b(B), .out(\Multiplicación ), .cout(C_M));  // open: cin
  Divider #(.width(32)) divider_1 (.a(A), .b(B), .out(\División ), .rem(Resto));  // open: upper
  assign Comp_Mayor = {{31{1'b0}}, comparator_1_gt};  // Bit_Extender bit_extender_1
  Comparator #(.width(32)) comparator_1 (.a(A), .b(B), .gt(comparator_1_gt));  // open: eq, lt
  Comparator #(.width(32)) comparator_2 (.a(A), .b(B), .lt(comparator_2_lt));  // open: gt, eq
  assign Comp_Menor = {{31{1'b0}}, comparator_2_lt};  // Bit_Extender bit_extender_2
  assign AND = A & B;  // AND_Gate and_1, 32 bits wide
  assign OR = A | B;  // OR_Gate or_1, 32 bits wide
  assign XOR = A ^ B;  // XOR_Gate xor_1, 32 bits wide
  assign NOT_A = ~A;  // NOT_Gate not_1, 32 bits wide
  assign NOT_B = ~B;  // NOT_Gate not_2, 32 bits wide
  Multiplexer #(.select(4), .width(32)) multiplexer_1 (
    .in0(Suma), .in1(Resta), .in2(\Multiplicación ), .in3(\División ), .in4(Resto), .in5(AND), .in6(OR),
    .in7(XOR), .in8(NOT_A), .in9(NOT_B), .in10(Comp_Mayor), .in11(Comp_Menor), .out(Salida),
    .sel(\Operación ), .en(Enable));  // open: in12, in13, in14, in15
  assign bit_extender_3_out = {{31{1'b0}}, CarryAdd};  // Bit_Extender bit_extender_3
  assign bit_extender_4_out = {{31{1'b0}}, CarrySub};  // Bit_Extender bit_extender_4
  Multiplexer #(.select(2), .width(32), .enable("false")) multiplexer_2 (
    .in0(bit_extender_3_out), .in1(bit_extender_4_out), .in2(C_M), .in3(Resto), .out(Acarreo),
    .sel(\Operación [1:0]));
  Comparator #(.width(32)) comparator_3 (.a(Salida), .b({32{1'b0}}), .gt(out_6), .eq(out_7), .lt(out_8));

  // Notes on the sheet:
  //   Entrada
  //   Unidad Aritmético Lógica
  //   Salida
  //   Acarreo
endmodule
