// Logisim project S-MIPS.circ as structural Verilog: 13 circuits, main circuit S-MIPS Board
module S_MIPS_Board (
  input  DESHABILITAR_DISPATCHER,
  output halt
);

  wire button_1_out, CLK, CS, d_ff_1_q, LCLR, LoadRAM, LoadRAMOn, LW, R_R_W, R_W, ram_dispatcher_1_finished,
       RCS, Reset_out, RST, TTY_EN;
  wire [2:0] KDB;
  wire [3:0] LMask, Mask, ram_1_read_time, ram_1_write_time, RMask;
  wire [6:0] KDB_DATA, TTY_DATA;
  wire [15:0] Addr, LAddr, RAddr;
  wire [31:0] I0, I1, I2, I3, LData, ram_1_data_out_0, ram_1_data_out_1, ram_1_data_out_2, ram_1_data_out_3,
       RI0, RI1, RI2, RI3;

  TTY #(.rows(25), .cols(80)) tty_1 (.data(TTY_DATA), .clk(CLK), .we(TTY_EN), .clr(RST));
  not not_1 (LoadRAMOn, ram_dispatcher_1_finished);
  RAM_Dispatcher ram_dispatcher_1 (
    .WriteTime(ram_1_write_time), .Clock(CLK), .Data(LData), .Address(LAddr), .Mask(LMask),
    .Finished(ram_dispatcher_1_finished), .Write(LW), .CLR(LCLR));
  Keyboard #(.buflen(64)) keyboard_1 (.clk(CLK), .re(KDB[0]), .avail(KDB[2]), .data(KDB_DATA));  // open: clr
  RAM ram_1 (
    .Address(RAddr), .Data_Out_0(ram_1_data_out_0), .Data_Out_1(ram_1_data_out_1),
    .Data_Out_2(ram_1_data_out_2), .Data_Out_3(ram_1_data_out_3), .Data_In_0(RI0), .Data_In_1(RI1),
    .Data_In_2(RI2), .Data_In_3(RI3), .Mask(RMask), .nRead_Write(R_R_W), .Chip_Select(RCS),
    .Read_Time(ram_1_read_time), .Reset(button_1_out), .Write_Time(ram_1_write_time));
  Button button_1 (.out(button_1_out));
  D_Flip_Flop d_ff_1 (.clk(CLK), .D(1'b1), .Q(d_ff_1_q), .reset(Reset_out));  // open: Qn, preset, en
  Button Reset (.out(Reset_out));
  S_MIPS s_mips_1 (
    .Kbd_Enable(KDB[0]), .Address(Addr), .Kbd_Clear(KDB[1]), .Kbd_Available(KDB[2]), .RAM_In_0(I0),
    .Kbd_ASCII_Data(KDB_DATA), .RAM_In_1(I1), .TTY_Enable(TTY_EN), .RAM_In_2(I2), .RAM_In_3(I3),
    .TTY_ASCII_Data(TTY_DATA), .Reset(RST), .RAM_Out_0(ram_1_data_out_0), .Clock(CLK),
    .RAM_Out_1(ram_1_data_out_1), .Stop(halt), .RAM_Out_2(ram_1_data_out_2), .RAM_Out_3(ram_1_data_out_3),
    .Mask(Mask), .Read_Time(ram_1_read_time), .Write_Time(ram_1_write_time), .nRead_Write(R_W),
    .Chip_Select(CS));
  D_Flip_Flop d_ff_2 (.clk(CLK), .D(d_ff_1_q), .Qn(LCLR), .reset(Reset_out));  // open: Q, preset, en
  or or_1 (RST, LCLR, LoadRAM);
  Clock clock_1 (.out(CLK));
  Multiplexer #(.width(32), .enable("false")) multiplexer_1 (.in0(I0), .in1(LData), .out(RI0), .sel(LoadRAM));
  Multiplexer #(.width(32), .enable("false")) multiplexer_2 (.in0(I1), .in1(LData), .out(RI1), .sel(LoadRAM));
  Multiplexer #(.width(32), .enable("false")) multiplexer_3 (.in0(I2), .in1(LData), .out(RI2), .sel(LoadRAM));
  Multiplexer #(.width(32), .enable("false")) multiplexer_4 (.in0(I3), .in1(LData), .out(RI3), .sel(LoadRAM));
  and and_1 (LoadRAM, ~DESHABILITAR_DISPATCHER, LoadRAMOn);  // AND_Gate
  Multiplexer #(.width(16), .enable("false")) multiplexer_5 (.in0(Addr), .in1(LAddr), .out(RAddr), .sel(LoadRAM));
  Multiplexer #(.width(4), .enable("false")) multiplexer_6 (.in0(Mask), .in1(LMask), .out(RMask), .sel(LoadRAM));
  Multiplexer #(.enable("false")) multiplexer_7 (.in0(CS), .in1(LW), .out(RCS), .sel(LoadRAM));
  Multiplexer #(.enable("false")) multiplexer_8 (.in0(R_W), .in1(LW), .out(R_R_W), .sel(LoadRAM));

  // Notes on the sheet:
  //   NO MODIFICAR
  //   Keyboard
endmodule

module RAM (
  input  [15:0] Address,
  input  [31:0] Data_In_0,
  input  [31:0] Data_In_1,
  input  [31:0] Data_In_2,
  input  [31:0] Data_In_3,
  input  [3:0] Mask,
  input  nRead_Write,
  input  Chip_Select,
  input  Reset,
  output [31:0] Data_Out_0,
  output [31:0] Data_Out_1,
  output [31:0] Data_Out_2,
  output [31:0] Data_Out_3,
  output [3:0] Read_Time,
  output [3:0] Write_Time
);

  wire and_2_out, and_3_out, and_4_out, and_5_out, and_6_out, and_7_out, and_8_out, and_9_out, Changed, CLK,
       comparator_2_eq, comparator_3_eq, comparator_4_eq, comparator_5_eq, comparator_6_eq, Count,
       demultiplexer_3_out0, Idle, Idle_q, Load, Load0, Load1, nand_1_out, or_1_out, or_2_out, or_3_out,
       or_4_out, or_5_out, or_6_out, or_7_out, or_8_out, or_9_out, or_10_out, Proc_q, Update_Mem, Zero_Time;
  wire [3:0] counter_1_q, multiplexer_1_out, subtractor_1_out;
  wire [31:0] register_1_q, register_2_q, register_3_q, register_4_q, register_5_q;

  // Probe on 4'b0011
  // Probe on 4'b0010
  Multiplexer #(.width(4), .enable("false")) multiplexer_1 (
    .in0(4'b0011), .in1(4'b0010), .out(multiplexer_1_out), .sel(nRead_Write));
  or or_1 (or_1_out, Idle, Update_Mem);
  or or_2 (or_2_out, ~Chip_Select, Reset);  // OR_Gate
  Subtractor #(.width(4)) subtractor_1 (.a(multiplexer_1_out), .b(4'b0010), .out(subtractor_1_out));  // open: bin, bout
  D_Flip_Flop u_Idle (.clk(CLK), .D(or_1_out), .Q(Idle_q), .preset(or_2_out));  // open: Qn, en, reset
  Demultiplexer #(.enable("false")) demultiplexer_1 (.out0(Idle), .out1(Load0), .in(Idle_q), .sel(Changed));
  // Probe on counter_1_q
  Counter #(.width(4), .max('hf)) counter_1 (
    .load(Load), .D(subtractor_1_out), .count(Count), .Q(counter_1_q), .clk(CLK), .clr(or_3_out));  // open: carry
  or or_3 (or_3_out, ~Chip_Select, Reset);  // OR_Gate
  Comparator #(.width(4), .mode("unsigned")) comparator_1 (
    .a(4'b0000), .b(counter_1_q), .eq(Zero_Time));  // open: gt, lt
  or or_4 (or_4_out, Count, Load0, Load1);
  Register #(.width(32)) register_1 (.D(Data_In_0), .en(Chip_Select), .Q(register_1_q), .clk(CLK), .clr(or_5_out));
  or or_5 (or_5_out, ~Chip_Select, Reset);  // OR_Gate
  Register #(.width(32)) register_2 (.D(Data_In_1), .en(Chip_Select), .Q(register_2_q), .clk(CLK), .clr(or_6_out));
  or or_6 (or_6_out, ~Chip_Select, Reset);  // OR_Gate
  Register #(.width(32)) register_3 (.D(Data_In_2), .en(Chip_Select), .Q(register_3_q), .clk(CLK), .clr(or_7_out));
  or or_7 (or_7_out, ~Chip_Select, Reset);  // OR_Gate
  Register #(.width(32)) register_4 (.D(Data_In_3), .en(Chip_Select), .Q(register_4_q), .clk(CLK), .clr(or_8_out));
  or or_8 (or_8_out, ~Chip_Select, Reset);  // OR_Gate
  Register #(.width(32)) register_5 (
    .D({{11{1'b1}}, nRead_Write, Mask, Address}), .en(Chip_Select), .Q(register_5_q), .clk(CLK),
    .clr(or_9_out));
  or or_9 (or_9_out, ~Chip_Select, Reset);  // OR_Gate
  D_Flip_Flop Proc (.clk(CLK), .D(or_4_out), .Q(Proc_q), .reset(or_10_out));  // open: Qn, preset, en
  or or_10 (or_10_out, ~Chip_Select, Reset);  // OR_Gate
  Demultiplexer #(.enable("false")) demultiplexer_2 (
    .out0(Count), .out1(Update_Mem), .in(demultiplexer_3_out0), .sel(Zero_Time));
  Demultiplexer #(.enable("false")) demultiplexer_3 (
    .out0(demultiplexer_3_out0), .out1(Load1), .in(Proc_q), .sel(Changed));
  Clock clock_1 (.out(CLK));
  Comparator #(.width(32)) comparator_2 (.a(register_1_q), .b(Data_In_0), .eq(comparator_2_eq));  // open: gt, lt
  Comparator #(.width(32)) comparator_3 (.a(register_2_q), .b(Data_In_1), .eq(comparator_3_eq));  // open: gt, lt
  Comparator #(.width(32)) comparator_4 (.a(register_3_q), .b(Data_In_2), .eq(comparator_4_eq));  // open: gt, lt
  Comparator #(.width(32)) comparator_5 (.a(register_4_q), .b(Data_In_3), .eq(comparator_5_eq));  // open: gt, lt
  Comparator #(.width(32)) comparator_6 (
    .a(register_5_q), .b({{11{1'b1}}, nRead_Write, Mask, Address}), .eq(comparator_6_eq));  // open: gt, lt
  nand nand_1 (nand_1_out, comparator_6_eq, comparator_2_eq, comparator_3_eq, comparator_4_eq, comparator_5_eq);
  and and_1 (Changed, nand_1_out, Chip_Select);
  or or_11 (Load, Count, Load1, Load0);
  and and_2 (and_2_out, Mask[0], Update_Mem, nRead_Write);
  and and_3 (and_3_out, Mask[1], Update_Mem, nRead_Write);
  and and_4 (and_4_out, Mask[2], Update_Mem, nRead_Write);
  and and_5 (and_5_out, Mask[3], Update_Mem, nRead_Write);
  RAM_part #(.addrWidth(16), .dataWidth(32), .bus("separate")) ram_1 (
    .addr(Address), .din(Data_In_0), .data(Data_Out_0), .str(and_2_out), .sel(Chip_Select), .clk(CLK),
    .ld(and_6_out), .clr(Reset));
  and and_6 (and_6_out, ~nRead_Write, Idle);  // AND_Gate
  RAM_part #(.addrWidth(16), .dataWidth(32), .bus("separate")) ram_2 (
    .addr(Address), .din(Data_In_1), .data(Data_Out_1), .str(and_3_out), .sel(Chip_Select), .clk(CLK),
    .ld(and_7_out), .clr(Reset));
  and and_7 (and_7_out, ~nRead_Write, Idle);  // AND_Gate
  RAM_part #(.addrWidth(16), .dataWidth(32), .bus("separate")) ram_3 (
    .addr(Address), .din(Data_In_2), .data(Data_Out_2), .str(and_4_out), .sel(Chip_Select), .clk(CLK),
    .ld(and_8_out), .clr(Reset));
  and and_8 (and_8_out, ~nRead_Write, Idle);  // AND_Gate
  RAM_part #(.addrWidth(16), .dataWidth(32), .bus("separate")) ram_4 (
    .addr(Address), .din(Data_In_3), .data(Data_Out_3), .str(and_5_out), .sel(Chip_Select), .clk(CLK),
    .ld(and_9_out), .clr(Reset));
  and and_9 (and_9_out, ~nRead_Write, Idle);  // AND_Gate

  assign Read_Time = 4'b0011;
  assign Write_Time = 4'b0010;

  // Other names for the same wires on the sheet: M0 = Mask[0]; M1 = Mask[1]; M2 = Mask[2]; M3 = Mask[3];
  //   RW = nRead_Write; CLR = Reset; CS = Chip_Select; Load2 = Count

  // Notes on the sheet:
  //   NO MODIFICAR
  //   excepto quizás los valores RT y WT
  //   BANK0
  //   BANK1
  //   BANK2
  //   BANK3
endmodule

module S_MIPS (
  input  Kbd_Available,
  input  [6:0] Kbd_ASCII_Data,
  input  [31:0] RAM_Out_0,
  input  [31:0] RAM_Out_1,
  input  Reset,
  input  [31:0] RAM_Out_2,
  input  Clock,
  input  [31:0] RAM_Out_3,
  input  [3:0] Read_Time,
  input  [3:0] Write_Time,
  output Kbd_Enable,
  output [15:0] Address,
  output Kbd_Clear,
  output TTY_Enable,
  output [6:0] TTY_ASCII_Data,
  output Stop,
  output [31:0] RAM_In_0,
  output [31:0] RAM_In_1,
  output [31:0] RAM_In_2,
  output [31:0] RAM_In_3,
  output [3:0] Mask,
  output nRead_Write,
  output Chip_Select
);

  wire data_path_1_can_t_pop, data_path_1_cant_push, data_path_1_hit, data_path_1_l_s_ram,
       data_path_1_pop_push, I_SP, L_SP, N_I, PC_E, R_I;
  wire [1:0] data_path_1_special_op;
  wire [2:0] S_D;
  wire [3:0] data_path_1_unit_op;

  Control_Unit control_unit_1 (
    .Special_Op(data_path_1_special_op), .Operation(data_path_1_unit_op), .Write_Time(Write_Time),
    .Reset(Reset), .Clock(Clock), .End_Hit0(data_path_1_hit), .pop_push(data_path_1_pop_push),
    .cant_push(data_path_1_cant_push), .can_t_pop(data_path_1_can_t_pop), .L_S_Ram(data_path_1_l_s_ram),
    .S_Data(S_D), .Chip_Select(Chip_Select), .RI(R_I), .NI(N_I), .PC_Eneable(PC_E), .Init_SP(I_SP),
    .Load_SP(L_SP), .Kbd_Enable(Kbd_Enable), .Kbd_Clear(Kbd_Clear), .TTY_Enable(TTY_Enable), .STOP(Stop),
    .R_W_Ram(nRead_Write));
  Data_Path data_path_1 (
    .IN0(RAM_Out_0), .IN1(RAM_Out_1), .IN2(RAM_Out_2), .IN3(RAM_Out_3), .Read_Time(Read_Time), .Reset(Reset),
    .Clk(Clock), .S_Data(S_D), .Init_SP(I_SP), .Load_SP(L_SP), .ReadInst(R_I), .NewInst(N_I),
    .PC_Enable(PC_E), .Find(Chip_Select), .Kbd_Available(Kbd_Available), .Kbd_ASCII_Data(Kbd_ASCII_Data),
    .R_W_Ram(nRead_Write), .Ou0(RAM_In_0), .Ou1(RAM_In_1), .Ou2(RAM_In_2), .Ou3(RAM_In_3),
    .Ram_Address(Address), .Mask(Mask), .TTY_ASCII_Data(TTY_ASCII_Data), .Unit_Op(data_path_1_unit_op),
    .Special_Op(data_path_1_special_op), .Hit(data_path_1_hit), .cant_push(data_path_1_cant_push),
    .can_t_pop(data_path_1_can_t_pop), .pop_push(data_path_1_pop_push), .L_S_Ram(data_path_1_l_s_ram));

  // Other names for the same wires on the sheet: CLK = Clock; CLR = Reset; CS = Chip_Select;
  //   KBD_AVAIL = Kbd_Available; KBD_CLR = Kbd_Clear; KBD_DATA[6:0] = Kbd_ASCII_Data; RAM_A[15:0] = Address;
  //   RAM_INPUT_0[31:0] = RAM_In_0; RAM_INPUT_1[31:0] = RAM_In_1; RAM_INPUT_2[31:0] = RAM_In_2;
  //   RAM_INPUT_3[31:0] = RAM_In_3; RAM_MASK[3:0] = Mask; RAM_OUTPUT_0[31:0] = RAM_Out_0;
  //   RAM_OUTPUT_1[31:0] = RAM_Out_1; RAM_OUTPUT_2[31:0] = RAM_Out_2; RAM_OUTPUT_3[31:0] = RAM_Out_3;
  //   RW = nRead_Write; TTY_DATA[6:0] = TTY_ASCII_Data

  // Notes on the sheet:
  //   RAM ADDRESS
  //   DATA FROM RAM
  //   DATA TO RAM
  //   DATA WRITE MASK
  //   RAM TIMING
  //   RAM CONTROL
  //   KEYBOARD
  //   TTY
  //   SEQUENCING
  //   S-MIPS
  //   ___________________________________________
endmodule

module RAM_Dispatcher (
  input  [3:0] WriteTime,
  input  Clock,
  input  CLR,
  output [31:0] Data,
  output [15:0] Address,
  output [3:0] Mask,
  output Finished,
  output Write
);

  wire demultiplexer_2_out1, demultiplexer_3_out1, End, IDLE_q, IncAddr, Load, or_1_out, or_2_out, While_q,
       WriteEnd;
  wire [3:0] counter_1_q;
  wire [31:0] CurrentAddress_q;

  Counter #(.width(32), .max('hffffffff)) CurrentAddress (
    .count(IncAddr), .Q({CurrentAddress_q[31:18], Address, CurrentAddress_q[1:0]}), .clk(Clock), .clr(CLR));  // open: load, D, carry
  or or_1 (or_1_out, IncAddr, demultiplexer_3_out1, Finished);
  D_Flip_Flop IDLE (.clk(Clock), .D(or_1_out), .Q(IDLE_q), .preset(CLR));  // open: Qn, en, reset
  Demultiplexer #(.enable("false")) demultiplexer_1 (.out0(Load), .out1(Finished), .in(IDLE_q), .sel(End));
  D_Flip_Flop While (.clk(Clock), .D(or_2_out), .Q(While_q), .reset(CLR));  // open: Qn, preset, en
  or or_2 (or_2_out, Write, Load);
  RAM_part #(.addrWidth(18), .dataWidth(32)) ram_1 (
    .addr({Address, CurrentAddress_q[1:0]}), .data(Data), .clk(Clock));  // open: sel, ld, clr
  Demultiplexer #(.enable("false")) demultiplexer_2 (
    .out0(Write), .out1(demultiplexer_2_out1), .in(While_q), .sel(WriteEnd));
  Decoder #(.select(2)) decoder_1 (
    .out0(Mask[0]), .out1(Mask[1]), .out2(Mask[2]), .out3(Mask[3]), .sel(CurrentAddress_q[1:0]));  // open: en
  Demultiplexer #(.enable("false")) demultiplexer_3 (
    .out0(IncAddr), .out1(demultiplexer_3_out1), .in(demultiplexer_2_out1), .sel(End));
  Counter #(.width(4), .max('hf)) counter_1 (
    .load(Load), .D(WriteTime), .count(Write), .Q(counter_1_q), .clk(Clock));  // open: carry, clr
  Comparator #(.width(32)) comparator_1 (.a(Data), .b({32{1'b1}}), .eq(End));  // open: gt, lt
  Comparator #(.width(4)) comparator_2 (.a(4'b0000), .b(counter_1_q), .eq(WriteEnd));  // open: gt, lt

  // Other names for the same wires on the sheet: CLK = Clock; Count = Write; WT[3:0] = WriteTime
endmodule

module Control_Unit (
  input  [1:0] Special_Op,
  input  [3:0] Operation,
  input  [3:0] Write_Time,
  input  Reset,
  input  Clock,
  input  End_Hit0,
  input  pop_push,
  input  cant_push,
  input  can_t_pop,
  input  L_S_Ram,
  output [2:0] S_Data,
  output Chip_Select,
  output RI,
  output NI,
  output PC_Eneable,
  output Init_SP,
  output Load_SP,
  output Kbd_Enable,
  output Kbd_Clear,
  output TTY_Enable,
  output STOP,
  output R_W_Ram
);

  wire Again1, Again2, Again3, Again4, Again5, Again6, Again7, Again8, Again9, Again10, Again11,
       comparator_1_eq, CS2, CS3, CS4, CS5, d_ff_2_q, d_ff_3_q, d_ff_9_q, demultiplexer_1_out0,
       demultiplexer_1_out1, demultiplexer_2_out0, demultiplexer_3_out1, demultiplexer_3_out2,
       demultiplexer_3_out3, demultiplexer_3_out5, demultiplexer_3_out7, demultiplexer_3_out8,
       demultiplexer_4_out0, demultiplexer_4_out1, demultiplexer_5_out0, demultiplexer_7_out0,
       demultiplexer_7_out1, demultiplexer_8_out0, demultiplexer_9_out0, demultiplexer_10_out0,
       demultiplexer_11_out1, demultiplexer_12_out1, L_SP2, or_3_out, or_4_out, or_7_out, or_10_out,
       or_11_out, or_12_out, or_13_out, SD3, SD3_1, Start, Writed;
  wire [3:0] counter_1_q, subtractor_1_out;

  not not_1 (Start, Reset);
  D_Flip_Flop IDLE (.clk(Clock), .D(demultiplexer_1_out0), .Q(Init_SP), .preset(Reset));  // open: Qn, en, reset
  or or_1 (Chip_Select, RI, CS2, CS3, CS4, CS5);
  or or_2 (PC_Eneable, Again1, Again2, Again3, Again4, Again5, Again6, Again7, Again8, Again9, Again10, Again11, TTY_Enable, Kbd_Enable);
  Demultiplexer #(.enable("false")) demultiplexer_1 (
    .out0(demultiplexer_1_out0), .out1(demultiplexer_1_out1), .in(or_3_out), .sel(Start));
  or or_3 (or_3_out, Init_SP, PC_Eneable);
  or or_4 (or_4_out, demultiplexer_2_out0, demultiplexer_1_out1);
  or or_5 (Load_SP, Init_SP, Again5, L_SP2);
  Priority_Encoder priority_encoder_1 (
    .in0(Again2), .in1(Again3), .in2(SD3), .in3(Again11), .in4(Kbd_Enable), .out(S_Data));  // open: in5, in6, in7, en_in, gs, en_out
  D_Flip_Flop d_ff_1 (.clk(Clock), .D(or_4_out), .Q(RI), .reset(Reset));  // open: Qn, preset, en
  Demultiplexer demultiplexer_2 (.out0(demultiplexer_2_out0), .out1(NI), .in(RI), .sel(End_Hit0));  // open: en
  or or_6 (SD3, SD3_1, Again9);
  or or_7 (or_7_out, CS3, CS5);
  Subtractor #(.width(4)) subtractor_1 (.a(Write_Time), .b(4'b0001), .out(subtractor_1_out));  // open: bin, bout
  D_Flip_Flop d_ff_2 (.clk(Clock), .D(or_7_out), .Q(d_ff_2_q), .reset(Reset));  // open: Qn, preset, en
  D_Flip_Flop d_ff_3 (.clk(Clock), .D(NI), .Q(d_ff_3_q), .reset(Reset));  // open: Qn, preset, en
  or or_8 (R_W_Ram, CS3, CS5);
  Counter #(.width(4), .max('hf)) counter_1 (
    .load(or_7_out), .D(subtractor_1_out), .count(d_ff_2_q), .Q(counter_1_q), .clk(Clock), .clr(Reset));  // open: carry
  Comparator #(.width(4), .mode("unsigned")) comparator_1 (
    .a(counter_1_q), .b(4'b0000), .eq(comparator_1_eq));  // open: gt, lt
  Demultiplexer #(.select(4)) demultiplexer_3 (
    .out0(Again1), .out1(demultiplexer_3_out1), .out2(demultiplexer_3_out2), .out3(demultiplexer_3_out3),
    .out4(Again3), .out5(demultiplexer_3_out5), .out6(Again8), .out7(demultiplexer_3_out7),
    .out8(demultiplexer_3_out8), .in(d_ff_3_q), .sel(Operation));  // open: out9, out10, out11, out12, out13, out14, out15, en
  nand nand_1 (Writed, comparator_1_eq, d_ff_2_q);
  or or_9 (Again2, demultiplexer_3_out1, demultiplexer_3_out2, demultiplexer_3_out3);
  Demultiplexer demultiplexer_4 (
    .out0(demultiplexer_4_out0), .out1(demultiplexer_4_out1), .in(demultiplexer_3_out5), .sel(pop_push));  // open: en
  Demultiplexer demultiplexer_5 (
    .out0(demultiplexer_5_out0), .out1(Again4), .in(demultiplexer_4_out0), .sel(can_t_pop));  // open: en
  Demultiplexer demultiplexer_6 (.out0(L_SP2), .out1(Again6), .in(demultiplexer_4_out1), .sel(cant_push));  // open: en
  Demultiplexer demultiplexer_7 (
    .out0(demultiplexer_7_out0), .out1(demultiplexer_7_out1), .in(demultiplexer_3_out7), .sel(L_S_Ram));  // open: en
  Demultiplexer #(.select(2)) demultiplexer_8 (
    .out0(demultiplexer_8_out0), .out1(Again11), .out2(TTY_Enable), .out3(Kbd_Enable),
    .in(demultiplexer_3_out8), .sel(Special_Op));  // open: en
  D_Flip_Flop d_ff_4 (.clk(Clock), .D(or_10_out), .Q(CS2), .reset(Reset));  // open: Qn, preset, en
  or or_10 (or_10_out, demultiplexer_9_out0, demultiplexer_5_out0);
  or or_11 (or_11_out, L_SP2, demultiplexer_11_out1);
  or or_12 (or_12_out, demultiplexer_10_out0, demultiplexer_7_out0);
  or or_13 (or_13_out, demultiplexer_7_out1, demultiplexer_12_out1);
  Demultiplexer demultiplexer_9 (.out0(demultiplexer_9_out0), .out1(SD3_1), .in(CS2), .sel(End_Hit0));  // open: en
  D_Flip_Flop d_ff_5 (.clk(Clock), .D(or_11_out), .Q(CS3), .reset(Reset));  // open: Qn, preset, en
  D_Flip_Flop d_ff_6 (.clk(Clock), .D(or_12_out), .Q(CS4), .reset(Reset));  // open: Qn, preset, en
  Demultiplexer demultiplexer_10 (.out0(demultiplexer_10_out0), .out1(Again9), .in(CS4), .sel(End_Hit0));  // open: en
  D_Flip_Flop d_ff_7 (.clk(Clock), .D(or_13_out), .Q(CS5), .reset(Reset));  // open: Qn, preset, en
  Demultiplexer demultiplexer_11 (.out0(Again7), .out1(demultiplexer_11_out1), .in(CS3), .sel(Writed));  // open: en
  Demultiplexer demultiplexer_12 (.out0(Again10), .out1(demultiplexer_12_out1), .in(CS5), .sel(Writed));  // open: en
  or or_14 (Kbd_Clear, demultiplexer_8_out0, d_ff_9_q);
  D_Flip_Flop d_ff_8 (.clk(Clock), .D(SD3_1), .Q(Again5), .reset(Reset));  // open: Qn, preset, en
  D_Flip_Flop d_ff_9 (.clk(Clock), .D(Kbd_Clear), .Q(d_ff_9_q), .reset(Reset));  // open: Qn, preset, en

  assign STOP = Kbd_Clear;

  // Other names for the same wires on the sheet: Again12 = TTY_Enable; c_prime_t_pop = can_t_pop;
  //   c_prime_t_push = cant_push; Clk = Clock; CS = Chip_Select; CS1 = RI; End_Hit = End_Hit0; KBD_CLR = Kbd_Clear;
  //   L_SP = Load_SP; I_SP = Init_SP; L_SP1 = Init_SP; L_SP3 = Again5; Load_Store = L_S_Ram; Op[3:0] = Operation;
  //   p_p = pop_push; Again = PC_Eneable; PC_E = PC_Eneable; R_W_Ram1 = CS3; R_W_Ram2 = CS5; S_O[1:0] = Special_Op;
  //   SD1 = Again2; SD2 = Again3; SD3_2 = Again9; SD4 = Again11; Again13 = Kbd_Enable; SD5 = Kbd_Enable;
  //   WT[3:0] = Write_Time

  // Notes on the sheet:
  //   Inputs
  //   Control Unit
  //   ___________________________________________
endmodule

module Data_Path (
  input  [31:0] IN0,
  input  [31:0] IN1,
  input  [31:0] IN2,
  input  [31:0] IN3,
  input  [3:0] Read_Time,
  input  Reset,
  input  Clk,
  input  [2:0] S_Data,
  input  Init_SP,
  input  Load_SP,
  input  ReadInst,
  input  NewInst,
  input  PC_Enable,
  input  Find,
  input  Kbd_Available,
  input  [6:0] Kbd_ASCII_Data,
  input  R_W_Ram,
  output [31:0] Ou0,
  output [31:0] Ou1,
  output [31:0] Ou2,
  output [31:0] Ou3,
  output [15:0] Ram_Address,
  output [3:0] Mask,
  output [6:0] TTY_ASCII_Data,
  output [3:0] Unit_Op,
  output [1:0] Special_Op,
  output Hit,
  output cant_push,
  output can_t_pop,
  output pop_push,
  output L_S_Ram
);

  wire and_2_out, and_3_out, E, H_L, Input_B, L_H_L, N, P, R_W_RF, Z;
  wire [1:0] OffSet;
  wire [2:0] B_Op;
  wire [3:0] A_Op;
  wire [4:0] DataAddress, Selector_A, Selector_B;
  wire [25:0] Jump;
  wire [31:0] Addr, B, bit_extender_1_out, Cnst, Data_In, Hi, Hi_Lo, Instruction, InstSave, Kybd, Lo,
       multiplexer_1_out, multiplexer_2_out, multiplexer_3_out, multiplexer_5_out, PC, PC_new, Rand;
  wire [31:7] A;

  Multiplexer #(.width(32)) multiplexer_1 (.in0(B), .in1(Cnst), .out(multiplexer_1_out), .sel(Input_B));  // open: en
  Register_File register_file_1 (
    .DI(Data_In), .L(Lo), .H(Hi), .Rd(DataAddress), .Rs(Selector_A), .Rt(Selector_B), .Clk(Clk),
    .Reset(Reset), .Load(L_H_L), .Select(H_L), .pop_push(pop_push), .Init_SP(Init_SP), .Load_SP(Load_SP),
    .R_W(R_W_RF), .DRs({A, TTY_ASCII_Data}), .DRt(B), .Hi_Lo(Hi_Lo));
  ALU alu_1 (
    .A({A, TTY_ASCII_Data}), .B(multiplexer_1_out), .Operation(A_Op), .out(Lo), .PF(P), .ZF(Z), .NF(N),
    .Equal(E), .Hi(Hi));
  and and_1 (L_H_L, Unit_Op[0], Unit_Op[1], ~Unit_Op[2], ~Unit_Op[3]);  // AND_Gate
  and and_2 (and_2_out, ~Unit_Op[0], Unit_Op[1], ~Unit_Op[2], ~Unit_Op[3]);  // AND_Gate
  and and_3 (and_3_out, Unit_Op[0], Unit_Op[1], Unit_Op[2], ~Unit_Op[3]);  // AND_Gate
  or or_1 (Input_B, and_2_out, and_3_out);
  Intruction_Decoder intruction_decoder_1 (
    .Constant(Cnst), .Jump(Jump), .Unit_Op(Unit_Op), .ALU_Op(A_Op), .Branch_Op(B_Op),
    .Special_Op(Special_Op), .S_A(Selector_A), .S_B(Selector_B), .DA(DataAddress), .Move_Lo_Hi(H_L),
    .pop_push(pop_push), .load_store(L_S_Ram), .Write_RF(R_W_RF), .Intruction(InstSave));
  and and_4 (Mask[0], ~OffSet[0], ~OffSet[1]);  // AND_Gate
  and and_5 (Mask[1], OffSet[0], ~OffSet[1]);  // AND_Gate
  and and_6 (Mask[2], ~OffSet[0], OffSet[1]);  // AND_Gate
  and and_7 (Mask[3], OffSet[0], OffSet[1]);
  Branch_Control branch_control_1 (
    .PC(PC), .Const(Cnst), .Destiny(Jump), .A({A, TTY_ASCII_Data}), .N(N), .Z(Z), .P(P), .Equal(E),
    .B_Op(B_Op), .PC_out(PC_new));
  Memory_Cache memory_cache_1 (
    .IN0(IN0), .IN1(IN1), .IN2(IN2), .IN3(IN3), .Addr(Addr), .CLK(Clk), .REST(Reset), .R_W(R_W_Ram),
    .Find(Find), .RT(Read_Time), .Instruction(Instruction), .Addr_Ram(Ram_Address), .OffSet(OffSet),
    .End_Hit(Hit));
  Register #(.width(32)) u_Instruction (.D(Instruction), .en(NewInst), .Q(InstSave), .clk(Clk), .clr(Reset));
  Random #(.width(32), .seed(8)) Random (.clk(Clk), .out(Rand), .clr(Reset));  // open: next
  Multiplexer #(.width(32)) multiplexer_2 (.in1(B), .out(multiplexer_2_out), .sel(L_S_Ram));  // open: in0, en
  Multiplexer #(.width(32)) multiplexer_3 (
    .in0(multiplexer_2_out), .in1({A, TTY_ASCII_Data}), .out(multiplexer_3_out), .sel(pop_push));  // open: en
  Multiplexer #(.select(3), .width(32)) multiplexer_4 (
    .in0(Lo), .in1(Hi_Lo), .in2(Instruction), .in3(Rand), .in4(Kybd), .out(Data_In), .sel(S_Data));  // open: in5, in6, in7, en
  Multiplexer #(.width(32)) multiplexer_5 (.in0(B), .in1(Lo), .out(multiplexer_5_out), .sel(Unit_Op[1]));  // open: en
  assign bit_extender_1_out = {{25{1'b0}}, Kbd_ASCII_Data};  // Bit_Extender bit_extender_1
  Demultiplexer #(.select(2), .width(32)) demultiplexer_1 (
    .out0(Ou0), .out1(Ou1), .out2(Ou2), .out3(Ou3),
    .in({multiplexer_3_out[7:0], multiplexer_3_out[15:8], multiplexer_3_out[23:16], multiplexer_3_out[31:24]}),
    .sel(OffSet));  // open: en
  Register #(.width(32)) u_PC (.D(PC_new), .en(PC_Enable), .Q(PC), .clk(Clk), .clr(Reset));
  Multiplexer #(.width(32)) multiplexer_6 (.in0(multiplexer_5_out), .in1(PC), .out(Addr), .sel(ReadInst));  // open: en
  Multiplexer #(.width(32)) multiplexer_7 (
    .in0({32{1'b1}}), .in1(bit_extender_1_out), .out(Kybd), .sel(Kbd_Available));  // open: en
  Comparator #(.width(32)) comparator_1 (.a(Addr), .b(32'h100000), .eq(can_t_pop));  // open: gt, lt
  Comparator #(.width(32)) comparator_2 (.a(Addr), .b(32'h1000), .eq(cant_push));  // open: gt, lt

  // Other names for the same wires on the sheet: A[6:0] = TTY_ASCII_Data; TTY_DATA[6:0] = TTY_ASCII_Data;
  //   c_prime_t_pop = can_t_pop; c_prime_t_push = cant_push; End = Hit; F = Find; I_SP = Init_SP;
  //   KBD_AVAIL = Kbd_Available; KBD_DATA[6:0] = Kbd_ASCII_Data; L_SP = Load_SP; Load_Store = L_S_Ram; NI = NewInst;
  //   P_P = pop_push; Ram_addr[15:0] = Ram_Address; RI = ReadInst; RT[3:0] = Read_Time; UO0 = Unit_Op[0];
  //   UO1 = Unit_Op[1]; UO2 = Unit_Op[2]; UO3 = Unit_Op[3]

  // Notes on the sheet:
  //   Inputs
  //   Data Path
  //   ___________________________________________
  //   Outputs
endmodule

module ALU (
  input  [31:0] A,
  input  [31:0] B,
  input  [3:0] Operation,
  output [31:0] out,
  output PF,
  output ZF,
  output NF,
  output Equal,
  output [31:0] Hi
);

  wire and_2_out, comparator_1_lt, comparator_2_lt;
  wire [31:0] add, \and , hi_div, hi_divu, hi_mul, hi_mulu, lo_div, lo_divu, lo_mul, lo_mulu, \nor , \or ,
       S_less, sub, U_less, \xor ;

  Multiplier #(.width(32)) multiplier_1 (.a(A), .b(B), .out(lo_mul), .cout(hi_mul));  // open: cin
  Mulu mulu_1 (.A(A), .B(B), .Lo(lo_mulu), .Hi(hi_mulu));
  Div div_1 (.A(A), .B(B), .Lo(lo_div), .Hi(hi_div));
  Comparator #(.width(32)) comparator_1 (.a(A), .b(B), .eq(Equal), .lt(comparator_1_lt));  // open: gt
  assign S_less = {{31{1'b0}}, comparator_1_lt};  // Bit_Extender bit_extender_1
  Adder #(.width(32)) adder_1 (.a(A), .b(B), .out(add));  // open: cin, cout
  Subtractor #(.width(32)) subtractor_1 (.a(A), .b(B), .out(sub));  // open: bin, bout
  Divider #(.width(32)) divider_1 (.a(A), .b(B), .out(lo_divu), .rem(hi_divu));  // open: upper
  Comparator #(.width(32), .mode("unsigned")) comparator_2 (.a(A), .b(B), .lt(comparator_2_lt));  // open: gt, eq
  assign \and  = A & B;  // AND_Gate and_1, 32 bits wide
  assign \or  = A | B;  // OR_Gate or_1, 32 bits wide
  assign \nor  = ~(A | B);  // NOR_Gate nor_1, 32 bits wide
  assign \xor  = A ^ B;  // XOR_Gate xor_1, 32 bits wide
  assign U_less = {{31{1'b0}}, comparator_2_lt};  // Bit_Extender bit_extender_2
  Multiplexer #(.select(4), .width(32), .enable("false")) multiplexer_1 (
    .in0({32{1'b0}}), .in1(A), .in2(S_less), .in3(U_less), .in4(lo_mul), .in5(lo_mulu), .in6(lo_div),
    .in7(lo_divu), .in8(add), .in9(sub), .in10(\and ), .in11(\or ), .in12(\nor ), .in13(\xor ), .out(out),
    .sel(Operation));  // open: in14, in15
  Multiplexer #(.select(2), .width(32)) multiplexer_2 (
    .in0(hi_mul), .in1(hi_mulu), .in2(hi_div), .in3(hi_divu), .out(Hi), .sel(Operation[1:0]), .en(and_2_out));
  and and_2 (and_2_out, Operation[2], ~Operation[3]);  // AND_Gate
  Comparator #(.width(32)) comparator_3 (.a(out), .b({32{1'b0}}), .gt(PF), .eq(ZF), .lt(NF));

  // Other names for the same wires on the sheet: Op[3:0] = Operation

  // Notes on the sheet:
  //   Inputs
  //   Aritmetic Logic Unit
  //   ___________________________________________
  //   Outputs
endmodule

module Mulu (
  input  [31:0] A,
  input  [31:0] B,
  output [31:0] Lo,
  output [31:0] Hi
);

  wire [31:0] adder_1_out, multiplexer_1_out, multiplexer_2_out, multiplier_1_cout;

  Multiplexer #(.width(32), .enable("false")) multiplexer_1 (
    .in0({32{1'b0}}), .in1(A), .out(multiplexer_1_out), .sel(B[31]));
  Multiplexer #(.width(32), .enable("false")) multiplexer_2 (
    .in0({32{1'b0}}), .in1(B), .out(multiplexer_2_out), .sel(A[31]));
  Adder #(.width(32)) adder_1 (.a(multiplexer_1_out), .b(multiplexer_2_out), .out(adder_1_out));  // open: cin, cout
  Multiplier #(.width(32)) multiplier_1 (.a(A), .b(B), .out(Lo), .cout(multiplier_1_cout));  // open: cin
  Adder #(.width(32)) adder_2 (.a(multiplier_1_cout), .b(adder_1_out), .out(Hi));  // open: cin, cout

  // Notes on the sheet:
  //   Inputs
  //   Mulu
  //   ___________________________________________
  //   Output
endmodule

module Div (
  input  [31:0] A,
  input  [31:0] B,
  output [31:0] Lo,
  output [31:0] Hi
);

  wire xor_1_out;
  wire [31:0] divider_1_out, multiplexer_1_out, multiplexer_2_out, negator_1_out, negator_2_out,
       negator_3_out;

  Negator #(.width(32)) negator_1 (.in(A), .out(negator_1_out));
  Negator #(.width(32)) negator_2 (.in(B), .out(negator_2_out));
  Multiplexer #(.width(32), .enable("false")) multiplexer_1 (
    .in0(A), .in1(negator_1_out), .out(multiplexer_1_out), .sel(A[31]));
  Multiplexer #(.width(32), .enable("false")) multiplexer_2 (
    .in0(B), .in1(negator_2_out), .out(multiplexer_2_out), .sel(B[31]));
  Divider #(.width(32)) divider_1 (
    .a(multiplexer_1_out), .b(multiplexer_2_out), .out(divider_1_out), .rem(Hi));  // open: upper
  xor xor_1 (xor_1_out, A[31], B[31]);
  Negator #(.width(32)) negator_3 (.in(divider_1_out), .out(negator_3_out));
  Multiplexer #(.width(32), .enable("false")) multiplexer_3 (
    .in0(divider_1_out), .in1(negator_3_out), .out(Lo), .sel(xor_1_out));

  // Notes on the sheet:
  //   Inputs
  //   Div
  //   ___________________________________________
  //   Output
endmodule

module Memory_Cache (
  input  [31:0] IN0,
  input  [31:0] IN1,
  input  [31:0] IN2,
  input  [31:0] IN3,
  input  [31:0] Addr,
  input  CLK,
  input  REST,
  input  R_W,
  input  Find,
  input  [3:0] RT,
  output [31:0] Instruction,
  output [15:0] Addr_Ram,
  output [1:0] OffSet,
  output End_Hit
);

  wire and_1_out, and_2_out, and_3_out, and_4_out, comparator_1_eq, comparator_2_eq, d_ff_1_q, en0, en1, en2,
       en3, en4, en5, en6, en7, nor_1_out, or_1_out, Ready_RT, V0, V1, V2, V3, V4, V5, V6, V7, Validated;
  wire [3:0] counter_1_q, subtractor_1_out;
  wire [12:0] T0, T1, T2, T3, T4, T5, T6, T7, TagCopy;
  wire [31:0] multiplexer_1_out, multiplexer_2_out, multiplexer_3_out, multiplexer_4_out, O0, O1, O2, O3, O4,
       O5, O6, O7, O8, O9, O10, O11, O12, O13, O14, O15, O16, O17, O18, O19, O20, O21, O22, O23, O24, O25,
       O26, O27, O28, O29, O30, O31;

  Multiplexer #(.select(3), .width(32), .enable("false")) multiplexer_1 (
    .in0(O0), .in1(O4), .in2(O8), .in3(O12), .in4(O16), .in5(O20), .in6(O24), .in7(O28),
    .out(multiplexer_1_out), .sel(Addr[6:4]));
  Multiplexer #(.select(3), .width(32), .enable("false")) multiplexer_2 (
    .in0(O3), .in1(O7), .in2(O11), .in3(O15), .in4(O19), .in5(O23), .in6(O27), .in7(O31),
    .out(multiplexer_2_out), .sel(Addr[6:4]));
  Register #(.width(13)) register_1 (.D(Addr[19:7]), .en(en0), .Q(T0), .clk(CLK), .clr(REST));
  Register #(.width(13)) register_2 (.D(Addr[19:7]), .en(en1), .Q(T1), .clk(CLK), .clr(REST));
  Register #(.width(13)) register_3 (.D(Addr[19:7]), .en(en2), .Q(T2), .clk(CLK), .clr(REST));
  Register #(.width(13)) register_4 (.D(Addr[19:7]), .en(en3), .Q(T3), .clk(CLK), .clr(REST));
  Register #(.width(13)) register_5 (.D(Addr[19:7]), .en(en4), .Q(T4), .clk(CLK), .clr(REST));
  Register #(.width(13)) register_6 (.D(Addr[19:7]), .en(en5), .Q(T5), .clk(CLK), .clr(REST));
  Register #(.width(13)) register_7 (.D(Addr[19:7]), .en(en6), .Q(T6), .clk(CLK), .clr(REST));
  Register #(.width(13)) register_8 (.D(Addr[19:7]), .en(en7), .Q(T7), .clk(CLK), .clr(REST));
  Multiplexer #(.select(3), .width(32), .enable("false")) multiplexer_3 (
    .in0(O1), .in1(O5), .in2(O9), .in3(O13), .in4(O17), .in5(O21), .in6(O25), .in7(O29),
    .out(multiplexer_3_out), .sel(Addr[6:4]));
  Multiplexer #(.select(3), .width(32), .enable("false")) multiplexer_4 (
    .in0(O2), .in1(O6), .in2(O10), .in3(O14), .in4(O18), .in5(O22), .in6(O26), .in7(O30),
    .out(multiplexer_4_out), .sel(Addr[6:4]));
  Multiplexer #(.select(2), .width(32), .enable("false")) multiplexer_5 (
    .in0(multiplexer_1_out), .in1(multiplexer_3_out), .in2(multiplexer_4_out), .in3(multiplexer_2_out),
    .out({Instruction[7:0], Instruction[15:8], Instruction[23:16], Instruction[31:24]}), .sel(Addr[3:2]));
  Register #(.width(32)) register_9 (.D(IN0), .en(en0), .Q(O0), .clk(CLK), .clr(REST));
  Register #(.width(32)) register_10 (.D(IN0), .en(en1), .Q(O4), .clk(CLK), .clr(REST));
  Register #(.width(32)) register_11 (.D(IN0), .en(en2), .Q(O8), .clk(CLK), .clr(REST));
  Register #(.width(32)) register_12 (.D(IN0), .en(en3), .Q(O12), .clk(CLK), .clr(REST));
  Register #(.width(32)) register_13 (.D(IN0), .en(en4), .Q(O16), .clk(CLK), .clr(REST));
  Register #(.width(32)) register_14 (.D(IN0), .en(en5), .Q(O20), .clk(CLK), .clr(REST));
  Register #(.width(32)) register_15 (.D(IN0), .en(en6), .Q(O24), .clk(CLK), .clr(REST));
  Register #(.width(32)) register_16 (.D(IN0), .en(en7), .Q(O28), .clk(CLK), .clr(REST));
  and and_1 (and_1_out, ~R_W, Find, ~End_Hit);  // AND_Gate
  and and_2 (and_2_out, and_1_out, ~Ready_RT);  // AND_Gate
  Register #(.width(32)) register_17 (.D(IN1), .en(en0), .Q(O1), .clk(CLK), .clr(REST));
  Register #(.width(32)) register_18 (.D(IN1), .en(en1), .Q(O5), .clk(CLK), .clr(REST));
  Register #(.width(32)) register_19 (.D(IN1), .en(en2), .Q(O9), .clk(CLK), .clr(REST));
  Register #(.width(32)) register_20 (.D(IN1), .en(en3), .Q(O13), .clk(CLK), .clr(REST));
  Register #(.width(32)) register_21 (.D(IN1), .en(en4), .Q(O17), .clk(CLK), .clr(REST));
  Register #(.width(32)) register_22 (.D(IN1), .en(en5), .Q(O21), .clk(CLK), .clr(REST));
  Register #(.width(32)) register_23 (.D(IN1), .en(en6), .Q(O25), .clk(CLK), .clr(REST));
  Register #(.width(32)) register_24 (.D(IN1), .en(en7), .Q(O29), .clk(CLK), .clr(REST));
  Subtractor #(.width(4)) subtractor_1 (.a(RT), .b(4'b0001), .out(subtractor_1_out));  // open: bin, bout
  D_Flip_Flop d_ff_1 (.clk(CLK), .D(and_2_out), .Q(d_ff_1_q), .reset(REST));  // open: Qn, preset, en
  Demultiplexer #(.select(3), .enable("false")) demultiplexer_1 (
    .out0(en0), .out1(en1), .out2(en2), .out3(en3), .out4(en4), .out5(en5), .out6(en6), .out7(en7),
    .in(or_1_out), .sel(Addr[6:4]));
  or or_1 (or_1_out, Ready_RT, R_W);
  Counter #(.width(4), .max('hf)) counter_1 (
    .load(and_1_out), .D(subtractor_1_out), .count(d_ff_1_q), .Q(counter_1_q), .clk(CLK), .clr(REST));  // open: carry
  Register #(.width(32)) register_25 (.D(IN2), .en(en0), .Q(O2), .clk(CLK), .clr(REST));
  Register #(.width(32)) register_26 (.D(IN2), .en(en1), .Q(O6), .clk(CLK), .clr(REST));
  Register #(.width(32)) register_27 (.D(IN2), .en(en2), .Q(O10), .clk(CLK), .clr(REST));
  Register #(.width(32)) register_28 (.D(IN2), .en(en3), .Q(O14), .clk(CLK), .clr(REST));
  Register #(.width(32)) register_29 (.D(IN2), .en(en4), .Q(O18), .clk(CLK), .clr(REST));
  Register #(.width(32)) register_30 (.D(IN2), .en(en5), .Q(O22), .clk(CLK), .clr(REST));
  Register #(.width(32)) register_31 (.D(IN2), .en(en6), .Q(O26), .clk(CLK), .clr(REST));
  Register #(.width(32)) register_32 (.D(IN2), .en(en7), .Q(O30), .clk(CLK), .clr(REST));
  nor nor_1 (nor_1_out, counter_1_q[0], counter_1_q[1], counter_1_q[2], counter_1_q[3]);
  and and_3 (and_3_out, nor_1_out, d_ff_1_q);
  Comparator #(.width(4), .mode("unsigned")) comparator_1 (.a(RT), .b(4'b0000), .eq(comparator_1_eq));  // open: gt, lt
  and and_4 (and_4_out, comparator_1_eq, Find);
  Register #(.width(32)) register_33 (.D(IN3), .en(en0), .Q(O3), .clk(CLK), .clr(REST));
  Register #(.width(32)) register_34 (.D(IN3), .en(en1), .Q(O7), .clk(CLK), .clr(REST));
  Register #(.width(32)) register_35 (.D(IN3), .en(en2), .Q(O11), .clk(CLK), .clr(REST));
  Register #(.width(32)) register_36 (.D(IN3), .en(en3), .Q(O15), .clk(CLK), .clr(REST));
  Register #(.width(32)) register_37 (.D(IN3), .en(en4), .Q(O19), .clk(CLK), .clr(REST));
  Register #(.width(32)) register_38 (.D(IN3), .en(en5), .Q(O23), .clk(CLK), .clr(REST));
  Register #(.width(32)) register_39 (.D(IN3), .en(en6), .Q(O27), .clk(CLK), .clr(REST));
  Register #(.width(32)) register_40 (.D(IN3), .en(en7), .Q(O31), .clk(CLK), .clr(REST));
  or or_2 (Ready_RT, and_3_out, and_4_out);
  D_Flip_Flop d_ff_2 (.clk(CLK), .D(Ready_RT), .Q(V0), .en(en0), .reset(REST));  // open: Qn, preset
  D_Flip_Flop d_ff_3 (.clk(CLK), .D(Ready_RT), .Q(V1), .en(en1), .reset(REST));  // open: Qn, preset
  D_Flip_Flop d_ff_4 (.clk(CLK), .D(Ready_RT), .Q(V2), .en(en2), .reset(REST));  // open: Qn, preset
  D_Flip_Flop d_ff_5 (.clk(CLK), .D(Ready_RT), .Q(V3), .en(en3), .reset(REST));  // open: Qn, preset
  D_Flip_Flop d_ff_6 (.clk(CLK), .D(Ready_RT), .Q(V4), .en(en4), .reset(REST));  // open: Qn, preset
  D_Flip_Flop d_ff_7 (.clk(CLK), .D(Ready_RT), .Q(V5), .en(en5), .reset(REST));  // open: Qn, preset
  D_Flip_Flop d_ff_8 (.clk(CLK), .D(Ready_RT), .Q(V6), .en(en6), .reset(REST));  // open: Qn, preset
  D_Flip_Flop d_ff_9 (.clk(CLK), .D(Ready_RT), .Q(V7), .en(en7), .reset(REST));  // open: Qn, preset
  Multiplexer #(.select(3), .enable("false")) multiplexer_6 (
    .in0(V0), .in1(V1), .in2(V2), .in3(V3), .in4(V4), .in5(V5), .in6(V6), .in7(V7), .out(Validated),
    .sel(Addr[6:4]));
  Comparator #(.width(13), .mode("unsigned")) comparator_2 (
    .a(TagCopy), .b(Addr[19:7]), .eq(comparator_2_eq));  // open: gt, lt
  and and_5 (End_Hit, comparator_2_eq, Validated);
  Multiplexer #(.select(3), .width(13), .enable("false")) multiplexer_7 (
    .in0(T0), .in1(T1), .in2(T2), .in3(T3), .in4(T4), .in5(T5), .in6(T6), .in7(T7), .out(TagCopy),
    .sel(Addr[6:4]));

  assign Addr_Ram = Addr[19:4];
  assign OffSet = Addr[3:2];

  // Other names for the same wires on the sheet: Index[2:0] = Addr[6:4]; Tag[12:0] = Addr[19:7]; F = Find;
  //   Reset = REST; Validate = Ready_RT

  // Notes on the sheet:
  //   IN2: pull=down
  //   IN3: pull=down
  //   IN1: pull=down
  //   Addr: pull=down
  //   IN0: pull=down
  //   Inputs
  //   Tag
  //   Return Instruction
  //   Cache
  //   ___________________________________________
  //   Cache
  //   Wait ReadTime
  //   put enable
  //   _____________________________________________________________________________
  //   _____________________________________________________________________________
  //   _____________________________________________________________________________
  //   _____________________________________________________________________________
  //   _____________________________________________________________________________
  //   _____________________________________________________________________________
  //   _____________________________________________________________________________
  //   Validate
  //   Search in Cache
  //   Outputs
endmodule

module Register_File (
  input  [31:0] DI,
  input  [31:0] L,
  input  [31:0] H,
  input  [4:0] Rd,
  input  [4:0] Rs,
  input  [4:0] Rt,
  input  Clk,
  input  Reset,
  input  Load,
  input  Select,
  input  pop_push,
  input  Init_SP,
  input  Load_SP,
  input  R_W,
  output [31:0] DRs,
  output [31:0] DRt,
  output [31:0] Hi_Lo
);

  wire L1, L2, L3, L4, L5, L6, L7, L8, L9, L10, L11, L12, L13, L14, L15, L16, L17, L18, L19, L20, L21, L22,
       L23, L24, L25, L26, L27, L28, L29, L30, LSP, LSP2;
  wire [31:0] adder_1_out, Hi, Lo, multiplexer_1_out, multiplexer_2_out, N_SP, Q0, Q1, Q2, Q3, Q4, Q5, Q6,
       Q7, Q8, Q9, Q10, Q11, Q12, Q13, Q14, Q15, Q16, Q17, Q18, Q19, Q20, Q21, Q22, Q23, Q24, Q25, Q26, Q27,
       Q28, Q29, Q30, QSP;

  Register #(.width(32)) R0 (.Q(Q0), .clk(Clk), .clr(Reset));  // open: D, en
  Register #(.width(32)) R4 (.D(DI), .en(L4), .Q(Q4), .clk(Clk), .clr(Reset));
  Register #(.width(32)) R8 (.D(DI), .en(L8), .Q(Q8), .clk(Clk), .clr(Reset));
  Register #(.width(32)) R12 (.D(DI), .en(L12), .Q(Q12), .clk(Clk), .clr(Reset));
  Register #(.width(32)) R16 (.D(DI), .en(L16), .Q(Q16), .clk(Clk), .clr(Reset));
  Register #(.width(32)) R20 (.D(DI), .en(L20), .Q(Q20), .clk(Clk), .clr(Reset));
  Register #(.width(32)) R24 (.D(DI), .en(L24), .Q(Q24), .clk(Clk), .clr(Reset));
  Register #(.width(32)) R28 (.D(DI), .en(L28), .Q(Q28), .clk(Clk), .clr(Reset));
  Register #(.width(32)) u_Lo (.D(L), .en(Load), .Q(Lo), .clk(Clk), .clr(Reset));
  Register #(.width(32)) R1 (.D(DI), .en(L1), .Q(Q1), .clk(Clk), .clr(Reset));
  Register #(.width(32)) R5 (.D(DI), .en(L5), .Q(Q5), .clk(Clk), .clr(Reset));
  Register #(.width(32)) R9 (.D(DI), .en(L9), .Q(Q9), .clk(Clk), .clr(Reset));
  Register #(.width(32)) R13 (.D(DI), .en(L13), .Q(Q13), .clk(Clk), .clr(Reset));
  Register #(.width(32)) R17 (.D(DI), .en(L17), .Q(Q17), .clk(Clk), .clr(Reset));
  Register #(.width(32)) R21 (.D(DI), .en(L21), .Q(Q21), .clk(Clk), .clr(Reset));
  Register #(.width(32)) R25 (.D(DI), .en(L25), .Q(Q25), .clk(Clk), .clr(Reset));
  Register #(.width(32)) R29 (.D(DI), .en(L29), .Q(Q29), .clk(Clk), .clr(Reset));
  Register #(.width(32)) u_Hi (.D(H), .en(Load), .Q(Hi), .clk(Clk), .clr(Reset));
  Register #(.width(32)) R2 (.D(DI), .en(L2), .Q(Q2), .clk(Clk), .clr(Reset));
  Register #(.width(32)) R6 (.D(DI), .en(L6), .Q(Q6), .clk(Clk), .clr(Reset));
  Register #(.width(32)) R10 (.D(DI), .en(L10), .Q(Q10), .clk(Clk), .clr(Reset));
  Register #(.width(32)) R14 (.D(DI), .en(L14), .Q(Q14), .clk(Clk), .clr(Reset));
  Register #(.width(32)) R18 (.D(DI), .en(L18), .Q(Q18), .clk(Clk), .clr(Reset));
  Register #(.width(32)) R22 (.D(DI), .en(L22), .Q(Q22), .clk(Clk), .clr(Reset));
  Register #(.width(32)) R26 (.D(DI), .en(L26), .Q(Q26), .clk(Clk), .clr(Reset));
  Register #(.width(32)) R30 (.D(DI), .en(L30), .Q(Q30), .clk(Clk), .clr(Reset));
  Multiplexer #(.width(32)) multiplexer_1 (
    .in0(32'h4), .in1(32'hfffffffc), .out(multiplexer_1_out), .sel(pop_push));  // open: en
  Register #(.width(32)) R3 (.D(DI), .en(L3), .Q(Q3), .clk(Clk), .clr(Reset));
  Register #(.width(32)) R7 (.D(DI), .en(L7), .Q(Q7), .clk(Clk), .clr(Reset));
  Register #(.width(32)) R11 (.D(DI), .en(L11), .Q(Q11), .clk(Clk), .clr(Reset));
  Register #(.width(32)) R15 (.D(DI), .en(L15), .Q(Q15), .clk(Clk), .clr(Reset));
  Register #(.width(32)) R19 (.D(DI), .en(L19), .Q(Q19), .clk(Clk), .clr(Reset));
  Register #(.width(32)) R23 (.D(DI), .en(L23), .Q(Q23), .clk(Clk), .clr(Reset));
  Register #(.width(32)) R27 (.D(DI), .en(L27), .Q(Q27), .clk(Clk), .clr(Reset));
  Register #(.width(32)) R31_SP (.D(N_SP), .en(LSP), .Q(QSP), .clk(Clk), .clr(Reset));
  Adder #(.width(32)) adder_1 (.a(multiplexer_1_out), .b(QSP), .out(adder_1_out));  // open: cin, cout
  Multiplexer #(.width(32)) multiplexer_2 (
    .in0(adder_1_out), .in1(32'h100000), .out(multiplexer_2_out), .sel(Init_SP));  // open: en
  Multiplexer #(.width(32)) multiplexer_3 (.in0(DI), .in1(multiplexer_2_out), .out(N_SP), .sel(Load_SP));  // open: en
  Multiplexer #(.select(5), .width(32)) multiplexer_4 (
    .in0(Q0), .in1(Q1), .in2(Q2), .in3(Q3), .in4(Q4), .in5(Q5), .in6(Q6), .in7(Q7), .in8(Q8), .in9(Q9),
    .in10(Q10), .in11(Q11), .in12(Q12), .in13(Q13), .in14(Q14), .in15(Q15), .in16(Q16), .in17(Q17),
    .in18(Q18), .in19(Q19), .in20(Q20), .in21(Q21), .in22(Q22), .in23(Q23), .in24(Q24), .in25(Q25),
    .in26(Q26), .in27(Q27), .in28(Q28), .in29(Q29), .in30(Q30), .in31(QSP), .out(DRs), .sel(Rs));  // open: en
  Multiplexer #(.select(5), .width(32)) multiplexer_5 (
    .in0(Q0), .in1(Q1), .in2(Q2), .in3(Q3), .in4(Q4), .in5(Q5), .in6(Q6), .in7(Q7), .in8(Q8), .in9(Q9),
    .in10(Q10), .in11(Q11), .in12(Q12), .in13(Q13), .in14(Q14), .in15(Q15), .in16(Q16), .in17(Q17),
    .in18(Q18), .in19(Q19), .in20(Q20), .in21(Q21), .in22(Q22), .in23(Q23), .in24(Q24), .in25(Q25),
    .in26(Q26), .in27(Q27), .in28(Q28), .in29(Q29), .in30(Q30), .in31(QSP), .out(DRt), .sel(Rt));  // open: en
  Demultiplexer #(.select(5)) demultiplexer_1 (
    .out1(L1), .out2(L2), .out3(L3), .out4(L4), .out5(L5), .out6(L6), .out7(L7), .out8(L8), .out9(L9),
    .out10(L10), .out11(L11), .out12(L12), .out13(L13), .out14(L14), .out15(L15), .out16(L16), .out17(L17),
    .out18(L18), .out19(L19), .out20(L20), .out21(L21), .out22(L22), .out23(L23), .out24(L24), .out25(L25),
    .out26(L26), .out27(L27), .out28(L28), .out29(L29), .out30(L30), .out31(LSP2), .in(R_W), .sel(Rd));  // open: out0, en
  or or_1 (LSP, LSP2, Load_SP);
  Multiplexer #(.width(32), .enable("false")) multiplexer_6 (.in0(Lo), .in1(Hi), .out(Hi_Lo), .sel(Select));

  // Other names for the same wires on the sheet: I_SP = Init_SP; LM_D = Load; LSP1 = Load_SP; Rst = Reset;
  //   Selector_H_L = Select

  // Notes on the sheet:
  //   Inputs
  //   Data in
  //   Low and high
  //   Data Address
  //   Selector A
  //   Selector B
  //   Clock
  //   Reset
  //   Read/Write
  //   Register File
  //   ___________________________________________
  //   Outputs
  //   Data out
endmodule

module Intruction_Decoder (
  input  [31:0] Intruction,
  output [31:0] Constant,
  output [25:0] Jump,
  output [3:0] Unit_Op,
  output [3:0] ALU_Op,
  output [2:0] Branch_Op,
  output [1:0] Special_Op,
  output [4:0] S_A,
  output [4:0] S_B,
  output [4:0] DA,
  output Move_Lo_Hi,
  output pop_push,
  output load_store,
  output Write_RF
);

  wire add, addi, \and , and_1_out, and_32_out, and_33_out, andi, beq, bgtz, blez, bltz, bne, div, divu,
       halt, j, jr, kbd, lw, mflo, mult, mulu, nop, \nor , \or , or_1_out, or_2_out, or_3_out, or_4_out,
       or_5_out, or_6_out, or_7_out, or_8_out, or_9_out, or_10_out, or_11_out, or_12_out, or_13_out,
       or_14_out, or_15_out, or_16_out, or_17_out, ori, pop, rnd, slt, slti, sltiu, sltu, sub, tty, \xor ,
       xori;
  wire [1:0] or_18_out, or_22_out;
  wire [15:0] bit_extender_1_out;

  assign bit_extender_1_out = {{15{Intruction[15]}}, Intruction[15]};  // Bit_Extender bit_extender_1
  or or_1 (or_1_out, andi, xori, ori);
  Multiplexer #(.width(16), .enable("false")) multiplexer_1 (
    .in0(bit_extender_1_out), .in1({16{1'b0}}), .out(Constant[31:16]), .sel(or_1_out));
  or or_2 (or_2_out, mult, mulu, div, divu);
  or or_3 (or_3_out, mflo, Move_Lo_Hi);
  or or_4 (or_4_out, add, \nor , sub, \xor , \and , slt, \or , sltu);
  or or_5 (or_5_out, addi, slti, andi, ori, sltiu, xori);
  or or_6 (or_6_out, pop, pop_push);
  or or_7 (or_7_out, beq, bltz, bne, j, blez, jr, bgtz);
  or or_8 (or_8_out, lw, load_store);
  or or_9 (or_9_out, halt, tty, rnd, kbd);
  Priority_Encoder #(.select(4)) priority_encoder_1 (
    .in0(nop), .in1(or_4_out), .in2(or_5_out), .in3(or_2_out), .in4(or_3_out), .in5(or_6_out),
    .in6(or_7_out), .in7(or_8_out), .in8(or_9_out), .out(Unit_Op));  // open: in9, in10, in11, in12, in13, in14, in15, gs, en_out, en_in
  and and_1 (and_1_out, ~Intruction[26], ~Intruction[27], ~Intruction[28], ~Intruction[29], ~Intruction[30], ~Intruction[31]);  // AND_Gate
  or or_10 (or_10_out, sltu, sltiu);
  or or_11 (or_11_out, lw, add, addi, load_store);
  or or_12 (or_12_out, \and , andi);
  or or_13 (or_13_out, \or , ori);
  and and_2 (add, ~Intruction[0], ~Intruction[1], ~Intruction[2], and_1_out, ~Intruction[3], ~Intruction[4], Intruction[5]);  // AND_Gate
  and and_3 (sub, ~Intruction[0], Intruction[1], ~Intruction[2], and_1_out, ~Intruction[3], ~Intruction[4], Intruction[5]);  // AND_Gate
  and and_4 (mult, ~Intruction[0], ~Intruction[1], ~Intruction[2], and_1_out, Intruction[3], Intruction[4], ~Intruction[5]);  // AND_Gate
  and and_5 (mulu, Intruction[0], ~Intruction[1], ~Intruction[2], and_1_out, Intruction[3], Intruction[4], ~Intruction[5]);  // AND_Gate
  and and_6 (div, ~Intruction[0], Intruction[1], ~Intruction[2], and_1_out, Intruction[3], Intruction[4], ~Intruction[5]);  // AND_Gate
  and and_7 (divu, Intruction[0], Intruction[1], ~Intruction[2], and_1_out, Intruction[3], Intruction[4], ~Intruction[5]);  // AND_Gate
  or or_14 (or_14_out, blez, bgtz, bltz);
  or or_15 (or_15_out, slt, slti);
  or or_16 (or_16_out, \xor , xori);
  Priority_Encoder #(.select(4)) priority_encoder_2 (
    .in0(1'b1), .in1(or_14_out), .in2(or_15_out), .in3(or_10_out), .in4(mult), .in5(mulu), .in6(div),
    .in7(divu), .in8(or_11_out), .in9(sub), .in10(or_12_out), .in11(or_13_out), .in12(\nor ),
    .in13(or_16_out), .out(ALU_Op));  // open: in14, in15, gs, en_out, en_in
  and and_8 (\and , ~Intruction[0], ~Intruction[1], Intruction[2], and_1_out, ~Intruction[3], ~Intruction[4], Intruction[5]);  // AND_Gate
  and and_9 (\or , Intruction[0], ~Intruction[1], Intruction[2], and_1_out, ~Intruction[3], ~Intruction[4], Intruction[5]);  // AND_Gate
  and and_10 (\nor , Intruction[0], Intruction[1], Intruction[2], and_1_out, ~Intruction[3], ~Intruction[4], Intruction[5]);  // AND_Gate
  and and_11 (\xor , ~Intruction[0], ~Intruction[1], ~Intruction[2], and_1_out, Intruction[3], ~Intruction[4], Intruction[5]);  // AND_Gate
  and and_12 (slt, ~Intruction[0], Intruction[1], ~Intruction[2], and_1_out, Intruction[3], ~Intruction[4], Intruction[5]);  // AND_Gate
  and and_13 (sltu, Intruction[0], Intruction[1], ~Intruction[2], and_1_out, Intruction[3], ~Intruction[4], Intruction[5]);  // AND_Gate
  Priority_Encoder #(.disabled(0)) priority_encoder_3 (
    .in0(1'b1), .in1(bne), .in2(blez), .in3(bgtz), .in4(bltz), .in5(j), .in6(jr), .in7(beq), .out(Branch_Op));  // open: en_in, gs, en_out
  or or_17 (or_17_out, add, sltu, sub, slti, mult, sltiu, mulu, beq, div, bne, divu, blez, addi, bgtz, bltz, \or , jr, \nor , lw, \xor , load_store, andi, pop_push, ori, tty, xori, \and , slt);
  and and_14 (Move_Lo_Hi, ~Intruction[0], ~Intruction[1], ~Intruction[2], and_1_out, ~Intruction[3], Intruction[4], ~Intruction[5]);  // AND_Gate
  and and_15 (mflo, ~Intruction[0], Intruction[1], ~Intruction[2], and_1_out, ~Intruction[3], Intruction[4], ~Intruction[5]);  // AND_Gate
  and and_16 (nop, ~Intruction[0], ~Intruction[1], ~Intruction[2], and_1_out, ~Intruction[3], ~Intruction[4], ~Intruction[5]);  // AND_Gate
  and and_17 (jr, ~Intruction[0], ~Intruction[1], ~Intruction[2], and_1_out, Intruction[3], ~Intruction[4], ~Intruction[5]);  // AND_Gate
  and and_18 (lw, Intruction[26], Intruction[27], ~Intruction[28], ~Intruction[29], ~Intruction[30], Intruction[31]);  // AND_Gate
  and and_19 (load_store, Intruction[26], Intruction[27], ~Intruction[28], Intruction[29], ~Intruction[30], Intruction[31]);  // AND_Gate
  Multiplexer #(.width(5), .enable("false")) multiplexer_2 (
    .in0({5{1'b0}}), .in1(Intruction[25:21]), .out(S_A), .sel(or_17_out));
  and and_20 (addi, ~Intruction[26], ~Intruction[27], ~Intruction[28], Intruction[29], ~Intruction[30], ~Intruction[31]);  // AND_Gate
  and and_21 (andi, ~Intruction[26], ~Intruction[27], Intruction[28], Intruction[29], ~Intruction[30], ~Intruction[31]);  // AND_Gate
  and and_22 (ori, Intruction[26], ~Intruction[27], Intruction[28], Intruction[29], ~Intruction[30], ~Intruction[31]);  // AND_Gate
  and and_23 (xori, ~Intruction[26], Intruction[27], Intruction[28], Intruction[29], ~Intruction[30], ~Intruction[31]);  // AND_Gate
  and and_24 (slti, ~Intruction[26], Intruction[27], ~Intruction[28], Intruction[29], ~Intruction[30], ~Intruction[31]);  // AND_Gate
  and and_25 (sltiu, Intruction[26], Intruction[27], ~Intruction[28], Intruction[29], ~Intruction[30], ~Intruction[31]);  // AND_Gate
  or or_18 (or_18_out[0], add, \nor , sub, \xor , mult, slt, mulu, sltu, div, beq, divu, bne, \and , load_store, \or );
  or or_19 (Special_Op[0], rnd, kbd);
  or or_20 (Special_Op[1], kbd, tty);
  Multiplexer #(.select(2), .width(5)) multiplexer_3 (
    .in0({5{1'b0}}), .in1(Intruction[20:16]), .in2({5{1'b1}}), .out(S_B), .sel(or_18_out));  // open: in3, en
  or or_21 (or_18_out[1], pop, pop_push);
  and and_26 (beq, ~Intruction[26], ~Intruction[27], Intruction[28], ~Intruction[29], ~Intruction[30], ~Intruction[31]);  // AND_Gate
  and and_27 (bne, Intruction[26], ~Intruction[27], Intruction[28], ~Intruction[29], ~Intruction[30], ~Intruction[31]);  // AND_Gate
  and and_28 (blez, ~Intruction[26], Intruction[27], Intruction[28], ~Intruction[29], ~Intruction[30], ~Intruction[31]);  // AND_Gate
  and and_29 (bgtz, Intruction[26], Intruction[27], Intruction[28], ~Intruction[29], ~Intruction[30], ~Intruction[31]);  // AND_Gate
  and and_30 (bltz, Intruction[26], ~Intruction[27], ~Intruction[28], ~Intruction[29], ~Intruction[30], ~Intruction[31]);  // AND_Gate
  and and_31 (j, ~Intruction[26], Intruction[27], ~Intruction[28], ~Intruction[29], ~Intruction[30], ~Intruction[31]);  // AND_Gate
  or or_22 (or_22_out[0], add, slt, sub, sltu, \and , Move_Lo_Hi, \or , mflo, \nor , pop, \xor , kbd, rnd);
  or or_23 (or_22_out[1], addi, slti, andi, sltiu, ori, lw, xori);
  and and_32 (and_32_out, ~Intruction[26], ~Intruction[27], ~Intruction[28], Intruction[29], Intruction[30], Intruction[31]);  // AND_Gate
  and and_33 (and_33_out, Intruction[26], Intruction[27], Intruction[28], Intruction[29], Intruction[30], Intruction[31]);
  Multiplexer #(.select(2), .width(5)) multiplexer_4 (
    .in0({5{1'b0}}), .in1(Intruction[15:11]), .in2(Intruction[20:16]), .out(DA), .sel(or_22_out));  // open: in3, en
  and and_34 (pop, ~Intruction[0], ~Intruction[1], ~Intruction[2], and_32_out, ~Intruction[3], ~Intruction[4], ~Intruction[5]);  // AND_Gate
  and and_35 (pop_push, Intruction[0], ~Intruction[1], ~Intruction[2], and_32_out, ~Intruction[3], ~Intruction[4], ~Intruction[5]);  // AND_Gate
  and and_36 (halt, Intruction[0], Intruction[1], Intruction[2], and_33_out, Intruction[3], Intruction[4], Intruction[5]);
  and and_37 (tty, Intruction[0], ~Intruction[1], ~Intruction[2], and_33_out, ~Intruction[3], ~Intruction[4], ~Intruction[5]);  // AND_Gate
  and and_38 (rnd, ~Intruction[0], Intruction[1], ~Intruction[2], and_33_out, ~Intruction[3], ~Intruction[4], ~Intruction[5]);  // AND_Gate
  and and_39 (kbd, ~Intruction[0], ~Intruction[1], Intruction[2], and_33_out, ~Intruction[3], ~Intruction[4], ~Intruction[5]);  // AND_Gate
  or or_24 (Write_RF, add, \xor , sub, slt, \and , sltu, \or , slti, \nor , sltiu, addi, pop, andi, lw, ori, rnd, xori, kbd, Move_Lo_Hi, mflo);

  assign Constant[15:0] = Intruction[15:0];
  assign Jump = Intruction[25:0];

  // Other names for the same wires on the sheet: Cons_Ext[31:0] = {Constant[31:16], Intruction[15:0]};
  //   Constant_t[15:0] = Intruction[15:0]; Destiny_Jump[25:0] = Intruction[25:0]; F1 = Intruction[0];
  //   Func_Code[5:0] = Intruction[5:0]; F2 = Intruction[1]; F3 = Intruction[2]; F4 = Intruction[3];
  //   F5 = Intruction[4]; F6 = Intruction[5]; Rd[4:0] = Intruction[15:11]; Rt[4:0] = Intruction[20:16];
  //   Rs[4:0] = Intruction[25:21]; O1 = Intruction[26]; Op_Code[5:0] = Intruction[31:26]; O2 = Intruction[27];
  //   O3 = Intruction[28]; O4 = Intruction[29]; O5 = Intruction[30]; O6 = Intruction[31]; Lo_Hi = Move_Lo_Hi;
  //   mfhi = Move_Lo_Hi; push = pop_push; sw = load_store; W_RF = Write_RF

  // Notes on the sheet:
  //   Inputs
  //   Ctrl Unit Operation
  //   ALU Operation
  //   Branch Operation
  //   Selector A
  //   Intruction Decoder
  //   ___________________________________________
  //   _____________________________________________________________________________
  //   _____________________________________________________________________________
  //   Selector B
  //   Special Operation
  //   Selector DA
  //   Write RF
  //   Outputs
endmodule

module Branch_Control (
  input  [31:0] PC,
  input  [31:0] Const,
  input  [25:0] Destiny,
  input  [31:0] A,
  input  N,
  input  Z,
  input  P,
  input  Equal,
  input  [2:0] B_Op,
  output [31:0] PC_out
);

  wire or_1_out;
  wire [31:0] beq, bgtz, blez, bltz, bne, Const_Ext, Jump, Standar;

  Shifter #(.width(32)) shifter_1 (.in(Const), .\dist (5'b00010), .out(Const_Ext));
  or or_1 (or_1_out, N, Z);
  Multiplexer #(.width(32)) multiplexer_1 (.in0(Standar), .in1(Jump), .out(beq), .sel(Equal));  // open: en
  Multiplexer #(.width(32)) multiplexer_2 (.in0(Standar), .in1(Jump), .out(blez), .sel(or_1_out));  // open: en
  Adder #(.width(32)) adder_1 (.a(PC), .b(32'h4), .out(Standar));  // open: cin, cout
  Multiplexer #(.width(32)) multiplexer_3 (.in0(Jump), .in1(Standar), .out(bne), .sel(Equal));  // open: en
  Multiplexer #(.width(32)) multiplexer_4 (.in0(Standar), .in1(Jump), .out(bgtz), .sel(P));  // open: en
  Multiplexer #(.select(3), .width(32)) multiplexer_5 (
    .in0(Standar), .in1(bne), .in2(blez), .in3(bgtz), .in4(bltz), .in5({PC[31:28], Destiny, 2'b00}), .in6(A),
    .in7(beq), .out(PC_out), .sel(B_Op));  // open: en
  Adder #(.width(32)) adder_2 (.a(Const_Ext), .b(Standar), .out(Jump));  // open: cin, cout
  Multiplexer #(.width(32)) multiplexer_6 (.in0(Standar), .in1(Jump), .out(bltz), .sel(N));  // open: en

  // Other names for the same wires on the sheet: J[31:2] = {PC[31:28], Destiny}

  // Notes on the sheet:
  //   B_Op: pull=down
  //   Z: pull=down
  //   N: pull=down
  //   Inputs
  //   Branch Control
  //   ___________________________________________
  //   Outputs
endmodule
